// Logisim project risc_cpu_simulation.circ as structural Verilog: 3 circuits, main circuit main
module main (
);

  wire [31:0] pc_v1_1_pc_out;

  PC_v1 pc_v1_1 (.PC_Out(pc_v1_1_pc_out));  // open: PC_In, PC_Select, Clk, Reset
  I_Memory_v1 i_memory_v1_1 (.Addr(pc_v1_1_pc_out));  // open: Clk, Stall, Instr
endmodule

module PC_v1 (
  input  [31:0] PC_In,
  input  PC_Select,
  input  Clk,
  input  Reset,
  output [31:0] PC_Out
);

  wire [31:0] adder_1_out, multiplexer_1_out;

  Adder #(.width(32)) adder_1 (.a(PC_Out), .b(32'h4), .out(adder_1_out));  // open: cin, cout
  Multiplexer #(.width(32)) multiplexer_1 (.in0(adder_1_out), .in1(PC_In), .out(multiplexer_1_out), .sel(PC_Select));
  Register #(.width(32)) register_1 (.D(multiplexer_1_out), .en(1'b1), .clk(Clk), .Q(PC_Out), .clr(Reset));
endmodule

module I_Memory_v1 (
  input  [31:0] Addr,
  input  Clk,
  output Stall,
  output [31:0] Instr
);

  ROM #(.addrWidth(16), .dataWidth(32)) rom_1 (.addr(Addr[15:0]), .data(Instr));

  assign Stall = 1'b0;
endmodule
